// Digital circuit 1x16 ram.dig as structural Verilog
module _1x16_ram (
  input  WS,
  input  CLK,
  input  [15:0] WD_15_0,
  input  RS1,
  input  RS2,
  output [15:0] RD1,
  output [15:0] RD2
);

  _1x1_Ram _1x1_ram_1 (.WD(WD_15_0[0]), .WS(WS), .RS1(RS1), .RS2(RS2), .CLK(CLK), .RD1(RD1[0]), .RD2(RD2[0]));
  _1x1_Ram _1x1_ram_2 (.WD(WD_15_0[8]), .WS(WS), .RS1(RS1), .RS2(RS2), .CLK(CLK), .RD1(RD1[8]), .RD2(RD2[8]));
  _1x1_Ram _1x1_ram_3 (.WD(WD_15_0[1]), .WS(WS), .RS1(RS1), .RS2(RS2), .CLK(CLK), .RD1(RD1[1]), .RD2(RD2[1]));
  _1x1_Ram _1x1_ram_4 (.WD(WD_15_0[9]), .WS(WS), .RS1(RS1), .RS2(RS2), .CLK(CLK), .RD1(RD1[9]), .RD2(RD2[9]));
  _1x1_Ram _1x1_ram_5 (.WD(WD_15_0[2]), .WS(WS), .RS1(RS1), .RS2(RS2), .CLK(CLK), .RD1(RD1[2]), .RD2(RD2[2]));
  _1x1_Ram _1x1_ram_6 (.WD(WD_15_0[10]), .WS(WS), .RS1(RS1), .RS2(RS2), .CLK(CLK), .RD1(RD1[10]), .RD2(RD2[10]));
  _1x1_Ram _1x1_ram_7 (.WD(WD_15_0[3]), .WS(WS), .RS1(RS1), .RS2(RS2), .CLK(CLK), .RD1(RD1[3]), .RD2(RD2[3]));
  _1x1_Ram _1x1_ram_8 (.WD(WD_15_0[11]), .WS(WS), .RS1(RS1), .RS2(RS2), .CLK(CLK), .RD1(RD1[11]), .RD2(RD2[11]));
  _1x1_Ram _1x1_ram_9 (.WD(WD_15_0[4]), .WS(WS), .RS1(RS1), .RS2(RS2), .CLK(CLK), .RD1(RD1[4]), .RD2(RD2[4]));
  _1x1_Ram _1x1_ram_10 (.WD(WD_15_0[12]), .WS(WS), .RS1(RS1), .RS2(RS2), .CLK(CLK), .RD1(RD1[12]), .RD2(RD2[12]));
  _1x1_Ram _1x1_ram_11 (.WD(WD_15_0[5]), .WS(WS), .RS1(RS1), .RS2(RS2), .CLK(CLK), .RD1(RD1[5]), .RD2(RD2[5]));
  _1x1_Ram _1x1_ram_12 (.WD(WD_15_0[13]), .WS(WS), .RS1(RS1), .RS2(RS2), .CLK(CLK), .RD1(RD1[13]), .RD2(RD2[13]));
  _1x1_Ram _1x1_ram_13 (.WD(WD_15_0[6]), .WS(WS), .RS1(RS1), .RS2(RS2), .CLK(CLK), .RD1(RD1[6]), .RD2(RD2[6]));
  _1x1_Ram _1x1_ram_14 (.WD(WD_15_0[14]), .WS(WS), .RS1(RS1), .RS2(RS2), .CLK(CLK), .RD1(RD1[14]), .RD2(RD2[14]));
  _1x1_Ram _1x1_ram_15 (.WD(WD_15_0[7]), .WS(WS), .RS1(RS1), .RS2(RS2), .CLK(CLK), .RD1(RD1[7]), .RD2(RD2[7]));
  _1x1_Ram _1x1_ram_16 (.WD(WD_15_0[15]), .WS(WS), .RS1(RS1), .RS2(RS2), .CLK(CLK), .RD1(RD1[15]), .RD2(RD2[15]));

  // Other names for the same wires on the sheet: WD0 = WD_15_0[0]; WD1 = WD_15_0[1]; WD2 = WD_15_0[2];
  //   WD3 = WD_15_0[3]; WD4 = WD_15_0[4]; WD5 = WD_15_0[5]; WD6 = WD_15_0[6]; WD7 = WD_15_0[7]; WD8 = WD_15_0[8];
  //   WD9 = WD_15_0[9]; WD10 = WD_15_0[10]; WD11 = WD_15_0[11]; WD12 = WD_15_0[12]; WD13 = WD_15_0[13];
  //   WD14 = WD_15_0[14]; WD15 = WD_15_0[15]
endmodule
