// Digital circuit 3bit Reg Set.dig as structural Verilog
module _3bit_Reg_Set (
  input  [1:0] WR_1_0,
  input  WE,
  input  [1:0] RA_1_0,
  input  [1:0] RB_1_0,
  input  [2:0] WRD_2_0,
  input  CLK,
  output [2:0] A_2_0,
  output [2:0] B_2_0
);

  wire A0, A1, A2, A3, D0, D1, D2, D3;
  wire [2:0] R0, R1, R2, R3;

  and and_1 (D0, WE, A0);
  and and_2 (D2, WE, A2);
  Decoder #(.Selector_Bits(2)) decoder_1 (.sel(WR_1_0), .out_0(A0), .out_1(A1), .out_2(A2), .out_3(A3));
  and and_3 (D1, WE, A1);
  and and_4 (D3, WE, A3);
  _3bit_Reg _3bit_reg_1 (.Din_2_0(WRD_2_0), .Sel(D3), .CLK(CLK), .Dout_2_0(R3));
  _3bit_Reg _3bit_reg_2 (.Din_2_0(WRD_2_0), .Sel(D2), .CLK(CLK), .Dout_2_0(R2));
  _3bit_Reg _3bit_reg_3 (.Din_2_0(WRD_2_0), .Sel(D1), .CLK(CLK), .Dout_2_0(R1));
  _3bit_Reg _3bit_reg_4 (.Din_2_0(WRD_2_0), .Sel(D0), .CLK(CLK), .Dout_2_0(R0));
  Multiplexer #(.Selector_Bits(2), .Bits(3)) multiplexer_1 (
    .sel(RA_1_0), .in_0(R0), .in_1(R1), .in_2(R2), .in_3(R3), .out(A_2_0));
  Multiplexer #(.Selector_Bits(2), .Bits(3)) multiplexer_2 (
    .sel(RB_1_0), .in_0(R0), .in_1(R1), .in_2(R2), .in_3(R3), .out(B_2_0));

  // Other names for the same wires on the sheet: RA[1:0] = RA_1_0; RB[1:0] = RB_1_0
endmodule
