// Digital circuit 3bitAdder.dig as structural Verilog
module _3bitAdder (
  input  [2:0] X_2_0,
  input  [2:0] Y_2_0,
  output Cout,
  output [2:0] R_2_0
);

  wire fa_2_cout, fa_3_cout;

  FA fa_1 (.X(X_2_0[2]), .Y(Y_2_0[2]), .Cin(fa_2_cout), .S(R_2_0[2]), .Cout(Cout));
  FA fa_2 (.X(X_2_0[1]), .Y(Y_2_0[1]), .Cin(fa_3_cout), .S(R_2_0[1]), .Cout(fa_2_cout));
  FA fa_3 (.X(X_2_0[0]), .Y(Y_2_0[0]), .Cin(1'b0), .S(R_2_0[0]), .Cout(fa_3_cout));
endmodule
