// Digital circuit 4bit_PC_reg.dig as structural Verilog
module _4bit_PC_reg (
  input  CLK,
  input  [3:0] I_3_0,
  output [3:0] O_3_0
);

  _1bit_Reg _1bit_reg_1 (.Din(I_3_0[0]), .Sel(1'b1), .CLK(CLK), .Dout(O_3_0[0]));
  _3bit_Reg _3bit_reg_1 (.Din_2_0(I_3_0[3:1]), .Sel(1'b1), .CLK(CLK), .Dout_2_0(O_3_0[3:1]));
endmodule
