// Digital circuit CPU.dig as structural Verilog
module CPU (
  input  CLK,
  input  [3:0] WR_3_0,
  input  WE,
  input  [15:0] WRD_15_0,
  input  PC_EN,
  input  [3:0] RA2_3_0,
  input  ZF,
  input  SF,
  output [15:0] RD_2,
  output [1:0] R1_1_0,
  output [1:0] R2_1_0,
  output [2:0] R_2_0,
  output [2:0] A_2_0,
  output [2:0] B_2_0,
  output [1:0] WR_1_0,
  output [3:0] JMP_ADDR
);

  wire CPU_CLK, Imm_SEL, JMP_SEL, Reg_EN;
  wire [1:0] Op;
  wire [2:0] _3bit_reg_set_1_b_2_0;
  wire [3:0] _4bit_pc_adder_1_o_3_0, _4bit_pc_reg_1_o_3_0, _9x16_sram_1_rd1_15_0, multiplexer_1_out;
  wire [7:0] Don_t_Care;

  Multiplexer #(.Bits(4)) multiplexer_1 (
    .sel(JMP_SEL), .in_0(_4bit_pc_adder_1_o_3_0), .in_1(JMP_ADDR), .out(multiplexer_1_out));
  and and_1 (CPU_CLK, PC_EN, CLK);
  _4bit_PC_Adder _4bit_pc_adder_1 (.I_3_0(_4bit_pc_reg_1_o_3_0), .O_3_0(_4bit_pc_adder_1_o_3_0));
  _4bit_PC_reg _4bit_pc_reg_1 (.I_3_0(multiplexer_1_out), .CLK(CPU_CLK), .O_3_0(_4bit_pc_reg_1_o_3_0));
  _9x16_SRAM _9x16_sram_1 (
    .RA1_3_0(_4bit_pc_reg_1_o_3_0), .RA2_3_0(RA2_3_0), .WR_3_0(WR_3_0), .WRD_15_0(WRD_15_0), .WE(WE),
    .CLK(CLK), .RD1_15_0({_9x16_sram_1_rd1_15_0, JMP_ADDR, Don_t_Care}), .RD2_15_0(RD_2));
  _3bit_Reg_Set _3bit_reg_set_1 (
    .WR_1_0(JMP_ADDR[3:2]), .CLK(CPU_CLK), .WE(Reg_EN), .WRD_2_0(R_2_0), .RA_1_0(JMP_ADDR[3:2]),
    .RB_1_0(JMP_ADDR[1:0]), .A_2_0(A_2_0), .B_2_0(_3bit_reg_set_1_b_2_0));
  CU cu_1 (
    .Opcode_3_0(_9x16_sram_1_rd1_15_0), .ZF(ZF), .SF(SF), .Op_1_0(Op), .REG_EN(Reg_EN), .Imm_Sel(Imm_SEL),
    .JMP_Sel(JMP_SEL));
  _3bitALU _3bitalu_1 (.A_2_0(A_2_0), .B_2_0(B_2_0), .R_2_0(R_2_0), .OP_1_0(Op));
  Multiplexer #(.Bits(3)) multiplexer_2 (
    .sel(Imm_SEL), .in_0(_3bit_reg_set_1_b_2_0), .in_1({JMP_ADDR[1:0], Don_t_Care[7]}), .out(B_2_0));

  assign R1_1_0 = JMP_ADDR[3:2];
  assign R2_1_0 = JMP_ADDR[1:0];
  assign WR_1_0 = JMP_ADDR[3:2];

  // Other names for the same wires on the sheet: Imm_Val[2:0] = {JMP_ADDR[1:0], Don_t_Care[7]};
  //   R2[1:0] = JMP_ADDR[1:0]; R1[1:0] = JMP_ADDR[3:2]; A[2:0] = A_2_0; B[2:0] = B_2_0; R[2:0] = R_2_0

  // Notes on the sheet:
  //   Register Mode (Type of Op = 00) => 2 bit (Type of op) + 2 bit (Op) + 2 bit (Reg1) + 2 bit (Reg2) + 8 bit (Don't Care)
  //   Immediate Mode (Type of Op = 01) => 2 bit (Type of op) + 2 bit (Op) + 2 bit (Reg1) + 3 bit (Imm Value) + 7 bit (Don't Care)
  //   Jump Mode (Type of Op = 10) => 2 bit (Type of op) + 4 bit (Addr) +  8 bit (Don't Care)
  //   Add (Op = 00), SHL (Op = 01), XOR (Op = 10)
  //   JMP (Op = 00), JLE (OP = 01)
  //   JMP START => 1000000100000000
  //   START: XOR R1, R1 => 0010010100000000
  //   JMPTO : ADD R1, 5    => 0100011010000000
  //   SHL R1, 1 => 0101010010000000
  //   JLE JMPTO => 1001001000000000
endmodule
